# Fritzing sketch Project 3 (saved by Fritzing 0.9.3b)
breadboards: 1

parts:
  Arduino = Arduino Uno (Rev3)
  Part2 = Thumb Joystick
  R3 = Resistor [tolerance=±5% resistance=10k package=THT]
  R4 = Resistor [tolerance=±5% resistance=10k package=THT]
  R5 = Resistor [tolerance=±5% resistance=10k package=THT]
  J1 = Basic Force Sensing Resistor (FSR) [package=THT]
  J2 = Basic Force Sensing Resistor (FSR) [package=THT]
  J3 = Basic Force Sensing Resistor (FSR) [package=THT]

nets:
  N1: Arduino.A0, Part2.VERT
  N2: Arduino.A1, Part2.HORZ
  N3: Arduino.A2, R3.Pin_0, J2.pin_1
  N4: Arduino.A3, R4.Pin_0, J1.pin_1
  N5: Arduino.A4/SDA, R5.Pin_0, J3.pin_1
  5V: Arduino.5V, Part2.VCC, J1.pin_0, J2.pin_0, J3.pin_0
  GND: Arduino.GND, Part2.GND, R3.Pin_1, R4.Pin_1, R5.Pin_1
